# Fritzing sketch led (saved by Fritzing 0.9.3b)
breadboards: 1

parts:
  Componente1 = Arduino Uno (Rev3)
  LED1 = LEDs [package=led10mm]
  R1 = Resistor [tolerance=±5% resistance=220 package=THT]

nets:
  N1: Componente1.D3_PWM, R1.Pin_0
  N2: Componente1.GND, LED1.C
  N3: LED1.A, R1.Pin_1
