# Fritzing sketch semaforo (saved by Fritzing 0.9.3b)
breadboards: 1

parts:
  Componente1 = Arduino Uno (Rev3)
  LED1 = LEDs [package=led10mm]
  LED2 = LEDs [package=led10mm]
  LED3 = LEDs [package=led10mm]
  LED4 = LEDs [package=led10mm]
  R1 = Resistor [tolerance=±5% resistance=220 package=THT]
  R2 = Resistor [tolerance=±5% resistance=220 package=THT]
  R3 = Resistor [tolerance=±5% resistance=220 package=THT]
  R4 = Resistor [tolerance=±5% resistance=220 package=THT]

nets:
  N1: Componente1.D3_PWM, R1.Pin_0
  N2: Componente1.D4, R2.Pin_0
  N3: Componente1.D5_PWM, R3.Pin_0
  N4: Componente1.D6_PWM, R4.Pin_0
  N5: Componente1.GND, LED1.C, LED2.C, LED3.C, LED4.C
  N6: LED1.A, R1.Pin_1
  N7: LED2.A, R2.Pin_1
  N8: LED3.A, R3.Pin_1
  N9: LED4.A, R4.Pin_1
